# Fritzing sketch simpleRobotShield (saved by Fritzing 0.9.3b)
breadboards: 1

parts:
  Part1 = Arduino Uno (Rev3)
  Q1 = Basic FET N-Channel [package="TO220 [THT]"]
  D2 = Rectifier Diode [part_number=1N4001 package="300 mil [THT]"]
  J1 = Screw terminal - 2 pins [package=THT]
  J2 = Screw terminal - 2 pins [package=THT]
  J3 = Screw terminal - 2 pins [package=THT]
  J4 = Screw terminal - 2 pins [package=THT]
  JP1 = Header 2 [package=screwterminal-3.5mm-2_lock]
  Q2 = Basic FET N-Channel [package="TO220 [THT]"]
  JP2 = Header 2 [package=screwterminal-3.5mm-2_lock]
  R1 = Resistor [tolerance=±5% resistance=220 package=THT]
  J5 = Screw terminal - 2 pins [package=THT]
  R2 = Resistor [tolerance=±5% resistance=220 package=THT]
  R3 = Resistor [tolerance=±5% resistance=220 package=THT]
  J6 = Screw terminal - 2 pins [package=THT]
  R4 = Resistor [tolerance=±5% resistance=220 package=THT]
  D13 = Diode [package=diode-1n4001]

nets:
  N1: Part1.A4/SDA, J6.pin2, R4.Pin_0
  N2: Part1.A5/SCL, J3.pin2, R3.Pin_0
  N3: Part1.D9_PWM, Q2.gate
  N4: Part1.D11_PWM/MOSI, Q1.gate
  N5: Part1.GND, Q1.source, J1.pin2, J4.pin2, Q2.source, R1.Pin_1, R2.Pin_1, R3.Pin_1, R4.Pin_1
  N6: Part1.D3_PWM, J5.pin1
  N7: Part1.D5_PWM, J2.pin1
  N8: Part1.5V, J3.pin1, J6.pin1
  N9: Part1.VIN, J1.pin1
  N10: Q1.drain, D2.anode, JP1.2
  N11: D2.cathode, J4.pin1, JP1.1, JP2.1, D13.C
  N12: J2.pin2, R1.Pin_0
  N13: Q2.drain, JP2.2, D13.A
  N14: J5.pin2, R2.Pin_0

notes:
  Left LDR
  Left motor
  Left LED
  Motor power
  Arduino power
  Right motor
  Right LED
  Right LDR
  Motor Power
